# Fritzing sketch final_setup (saved by Fritzing 0.9.4)
breadboards: 1

parts:
  Air_Pump = DC Motor
  Darlington_Transistor_1 = ULN2003A [package="SO16 [SMD]"]
  Valve_1 = Solenoid
  Raspberry_Pi_4B+ = Raspberry Pi B+
  Valve_2 = Solenoid
  Valve_3 = Solenoid
  Valve_4 = Solenoid
  Valve_5 = Solenoid
  Valve_6 = Solenoid
  Valve_7 = Solenoid
  Valve_8 = Solenoid
  Valve_9 = Solenoid
  Valve_10 = Solenoid
  Valve_11 = Solenoid
  Valve_12 = Solenoid
  Valve_13 = Solenoid
  Valve_14 = Solenoid
  Valve_15 = Solenoid
  Valve_16 = Solenoid
  Valve_17 = Solenoid
  Valve_18 = Solenoid
  Valve_19 = Solenoid
  Valve_20 = Solenoid
  Darlington_Transistor_2 = ULN2003A [package="SO16 [SMD]"]
  Darlington_Transistor_3 = ULN2003A [package="SO16 [SMD]"]
  Clock = ZS-042 RTC Module
  12V_Battery = 12V Battery

nets:
  N1: Air_Pump.pin_1, Raspberry_Pi_4B+.5V
  N2: Air_Pump.pin_2, Darlington_Transistor_2.Out_7
  N3: Darlington_Transistor_1.In_1, Raspberry_Pi_4B+.GPIO26
  N4: Darlington_Transistor_1.In_2, Raspberry_Pi_4B+.GPIO19
  N5: Darlington_Transistor_1.In_3, Raspberry_Pi_4B+.GPIO13
  N6: Darlington_Transistor_1.In_4, Raspberry_Pi_4B+.GPIO6
  N7: Darlington_Transistor_1.In_5, Raspberry_Pi_4B+.GPIO5
  N8: Darlington_Transistor_1.In_6, Raspberry_Pi_4B+.ID_SD
  N9: Darlington_Transistor_1.In_7, Raspberry_Pi_4B+.GPIO11
  GND: Darlington_Transistor_1.0V, Raspberry_Pi_4B+.GND, Darlington_Transistor_2.0V, Darlington_Transistor_3.0V, Clock.GND
  N10: Darlington_Transistor_1.COM_-_Common, Darlington_Transistor_2.COM_-_Common, Darlington_Transistor_3.COM_-_Common, 12V_Battery.+
  N11: Darlington_Transistor_1.Out_7, Valve_7.pin2
  N12: Darlington_Transistor_1.Out_6, Valve_6.pin2
  N13: Darlington_Transistor_1.Out_5, Valve_5.pin2
  N14: Darlington_Transistor_1.Out_4, Valve_4.pin2
  N15: Darlington_Transistor_1.Out_3, Valve_3.pin2
  N16: Darlington_Transistor_1.Out_2, Valve_2.pin2
  N17: Darlington_Transistor_1.Out_1, Valve_1.pin2
  N18: Valve_1.pin1, Valve_2.pin1, Valve_4.pin1, Valve_5.pin1, Valve_6.pin1, Valve_7.pin1, Valve_8.pin1, Valve_9.pin1, Valve_10.pin1, Valve_11.pin1, Valve_12.pin1, Valve_13.pin1, Valve_14.pin2, Valve_15.pin2, Valve_16.pin2, Valve_17.pin2, Valve_18.pin2, Valve_19.pin2, Valve_20.pin2, 12V_Battery.-
  3V3: Raspberry_Pi_4B+.3v3, Raspberry_Pi_4B+.3V3, Clock.VCC
  N19: Raspberry_Pi_4B+.GPIO2, Clock.SDA
  N20: Raspberry_Pi_4B+.GPIO3, Clock.SCL
  N21: Raspberry_Pi_4B+.GPIO4, Darlington_Transistor_2.In_6
  N22: Raspberry_Pi_4B+.GPIO17, Darlington_Transistor_2.In_5
  N23: Raspberry_Pi_4B+.GPIO27, Darlington_Transistor_2.In_4
  N24: Raspberry_Pi_4B+.GPIO22, Darlington_Transistor_2.In_3
  N25: Raspberry_Pi_4B+.GPIO10, Darlington_Transistor_2.In_2
  N26: Raspberry_Pi_4B+.GPIO9, Darlington_Transistor_2.In_1
  N27: Raspberry_Pi_4B+.GPIO21, Darlington_Transistor_2.In_7
  N28: Raspberry_Pi_4B+.GPIO8, Darlington_Transistor_3.In_1
  N29: Raspberry_Pi_4B+.GPIO25, Darlington_Transistor_3.In_2
  N30: Raspberry_Pi_4B+.GPIO24, Darlington_Transistor_3.In_3
  N31: Raspberry_Pi_4B+.GPIO23, Darlington_Transistor_3.In_4
  N32: Raspberry_Pi_4B+.GPIO18, Darlington_Transistor_3.In_5
  N33: Raspberry_Pi_4B+.GPIO15, Darlington_Transistor_3.In_6
  N34: Raspberry_Pi_4B+.GPIO14, Darlington_Transistor_3.In_7
  N35: Valve_8.pin2, Darlington_Transistor_2.Out_1
  N36: Valve_9.pin2, Darlington_Transistor_2.Out_2
  N37: Valve_10.pin2, Darlington_Transistor_2.Out_3
  N38: Valve_11.pin2, Darlington_Transistor_2.Out_4
  N39: Valve_12.pin2, Darlington_Transistor_2.Out_5
  N40: Valve_13.pin2, Darlington_Transistor_2.Out_6
  N41: Valve_14.pin1, Darlington_Transistor_3.Out_7
  N42: Valve_15.pin1, Darlington_Transistor_3.Out_6
  N43: Valve_16.pin1, Darlington_Transistor_3.Out_5
  N44: Valve_17.pin1, Darlington_Transistor_3.Out_4
  N45: Valve_18.pin1, Darlington_Transistor_3.Out_3
  N46: Valve_19.pin1, Darlington_Transistor_3.Out_2
  N47: Valve_20.pin1, Darlington_Transistor_3.Out_1

custom parts:
  12V Battery: A 4 x AAA battery pack (4.8 Volts with recharables)
