# Fritzing sketch setup_GPS (saved by Fritzing 0.9.4)
breadboards: 1

parts:
  Raspberry_Pi_4B+ = Raspberry Pi B+
  E218213_GPS_module = mystery part, 9 pins [chip_label=?]

nets:
  3V3: Raspberry_Pi_4B+.3v3, Raspberry_Pi_4B+.3V3, E218213_GPS_module.pin8
  N1: Raspberry_Pi_4B+.GND, E218213_GPS_module.pin7
  N2: Raspberry_Pi_4B+.GPIO15, E218213_GPS_module.pin5
  N3: Raspberry_Pi_4B+.GPIO14, E218213_GPS_module.pin6
