# Fritzing sketch setup_RTC (saved by Fritzing 0.9.4)

parts:
  Clock = ZS-042 RTC Module
  Raspberry_Pi_4B+ = Raspberry Pi B+

nets:
  GND: Clock.GND, Raspberry_Pi_4B+.GND
  3V3: Clock.VCC, Raspberry_Pi_4B+.3v3, Raspberry_Pi_4B+.3V3
  N1: Clock.SDA, Raspberry_Pi_4B+.GPIO2
  N2: Clock.SCL, Raspberry_Pi_4B+.GPIO3
